# Fritzing sketch schema_contatore-esp3 (saved by Fritzing 0.9.3b)
breadboards: 1

parts:
  Componente1 = Arduino Board Ethernet
  R1 = Resistor [tolerance=±5% resistance=330 package=THT]
  7_Segment1 = 7 Segment Display

nets:
  N1: Componente1.D8, 7_Segment1.Segment_F
  N2: Componente1.D9_PWM, 7_Segment1.Segment_G
  N3: Componente1.D2_PWM, 7_Segment1.Segment_A
  N4: Componente1.D3_PWM, 7_Segment1.Segment_B
  N5: Componente1.D5_PWM, 7_Segment1.Segment_C
  N6: Componente1.D6_PWM, 7_Segment1.Segment_D
  N7: Componente1.D7, 7_Segment1.Segment_E
  N8: Componente1.5V, R1.Pin_1
  N9: R1.Pin_0, 7_Segment1.common_anode
